# Fritzing sketch Leaf (saved by Fritzing 0.8.7b)
perfboards: 1

parts:
  U1 = NodeMCU V3.0
  ZS-042_RTC1 = ZS-042 RTC Module
  YF-S201_Flow_Meter1 = YF-S201 Water Flow Meter
  Part1 = FC-28 Soil Hygrometer Module
  Part2 = FC-28 Soil Hygrometer Module - Probe
  J1 = female pin header, 15 pins [form="♀ (female)"]
  J2 = female pin header, 15 pins [form="♀ (female)"]  # not connected
  J4 = female pin header, 6 pins [form="♀ (female)"]  # not connected
  J5 = female pin header, 6 pins [form="♀ (female)"]
  J6 = female pin header, 8 pins [form="♀ (female)"]
  J7 = female pin header, 6 pins [form="♀ (female)"]
  J8 = female pin header, 4 pins [form="♀ (female)"]
  J9 = male pin header, 2 pins [form="♂ (male)"]
  J3 = female pin header, 2 pins [form="♀ (female)"]
  J10 = female pin header, 6 pins [form="♀ (female)"]  # not connected

nets:
  N1: U1.D1, ZS-042_RTC1.SCL
  N2: U1.D2, ZS-042_RTC1.SDA
  N3: U1.D7, YF-S201_Flow_Meter1.GND
  VIN: U1.Vin, Part1.VCC
  N4: U1.A0, Part1.AO
  N5: ZS-042_RTC1.GND, YF-S201_Flow_Meter1.SIG, Part1.DO
  VCC: ZS-042_RTC1.VCC, YF-S201_Flow_Meter1.VCC
  N6: Part1.POS, Part2.POS
  N7: Part1.NEG, Part2.NEG
  N8: J1.pin2, J6.pin4, J8.pin3
  N9: J1.pin3, J6.pin3, J8.pin4
  N10: J1.pin8, J6.pin6, J7.pin1
  N11: J1.pin9, J6.pin8, J7.pin2
  N12: J1.pin10, J6.pin7, J7.pin3
  N13: J1.pin11, J6.pin5, J7.pin4
  N14: J5.pin3, J9.pin2
  N15: J5.pin4, J9.pin1
  N16: J5.pin5, J3.pin2
  N17: J5.pin6, J3.pin1

custom parts:
  NodeMCU V3.0: ESP8266 based NodeMCU
  YF-S201 Water Flow Meter: The YF-S201 Flow Meter. The input voltage is 5V to 24V (DC).
  FC-28 Soil Hygrometer Module: The FC-28 is a soil hygrometer module that uses the Texas Instruments LM393 comparator chip to provide an analog measurement of soil humidity. The digital output is high when soil moisture is over a certain threshold, as determined by adjusting the potentiometer.
  FC-28 Soil Hygrometer Module - Probe: The FC-28 is a soil hygrometer module that uses the Texas Instruments LM393 comparator chip to provide an analog measurement of soil humidity.
