# Fritzing sketch Relay Expansion Board (saved by Fritzing 0.8.7b)
circuit board: 8.46667cm x 5.64444cm
perfboards: 1

parts:
  U3 = 74HC595 [package="DIP16 [THT]"]
  J2 = female pin header, 8 pins [form="♀ (female)"]
  U4 = 74HC595 [package="DIP16 [THT]"]
  J3 = female pin header, 8 pins [form="♀ (female)"]
  J4 = female pin header, 3 pins [form="♀ (female)"]

nets:
  N1: U3.Q1, J2.pin7
  N2: U3.Q2, J2.pin6
  N3: U3.Q3, J2.pin5
  N4: U3.Q4, J2.pin4
  N5: U3.Q5, J2.pin3
  N6: U3.Q6, J2.pin2
  N7: U3.Q7, J2.pin1
  GND: U3.GND, U4.GND
  N8: U3.Q7', U4.DS
  N9: U3.MR, U3.VCC
  N10: U3.SH_CP, U4.SH_CP, J4.pin1
  N11: U3.ST_CP, U4.ST_CP, J4.pin2
  N12: U3.DS, J4.pin3
  N13: U3.Q0, J2.pin8
  N14: U4.Q1, J3.pin7
  N15: U4.Q2, J3.pin6
  N16: U4.Q3, J3.pin5
  N17: U4.Q4, J3.pin4
  N18: U4.Q5, J3.pin3
  N19: U4.Q6, J3.pin2
  N20: U4.Q7, J3.pin1
  N21: U4.MR, U4.VCC
  N22: U4.Q0, J3.pin8

notes:
  VCC
