# Fritzing sketch Root Diagram (saved by Fritzing 0.8.7b)
circuit board: 8.46667cm x 5.64444cm

parts:
  Part1 = Arduino Nano (Rev3.0)
  ZS-042_RTC1 = ZS-042 RTC Module
  U1 = NodeMCU V3.0
  8_Channel_Relay1 = 8 Channel Power Relay

nets:
  N1: Part1.D1/TX, Part1.D0/RX, U1.RX, U1.TX
  N2: Part1.D2, 8_Channel_Relay1.IN1
  N3: Part1.D3, 8_Channel_Relay1.IN2
  N4: Part1.D4, 8_Channel_Relay1.IN3
  N5: Part1.D5, 8_Channel_Relay1.IN4
  N6: Part1.D6, 8_Channel_Relay1.IN5
  N7: Part1.D7, 8_Channel_Relay1.IN6
  N8: Part1.D8, 8_Channel_Relay1.IN7
  N9: Part1.D9, 8_Channel_Relay1.IN8
  GND: Part1.GND, ZS-042_RTC1.GND
  5V: Part1.5V, ZS-042_RTC1.VCC
  N10: ZS-042_RTC1.SDA, U1.D2
  N11: ZS-042_RTC1.SCL, U1.D0, U1.D1
  VIN: U1.Vin, 8_Channel_Relay1.VCC

custom parts:
  NodeMCU V3.0: ESP8266 based NodeMCU
  8 Channel Power Relay: An 8 channel power relay. The module operates at 5V.
