# Fritzing sketch SARIBO Leaf April 5, 2020 Design (saved by Fritzing 0.8.7b)

parts:
  U1 = NodeMCU V3.0
  DS3231_RTC_Module1 = DS3231 RTC Module
  Part1 = MicroSD Card Module
  Part2 = FC-28 Soil Hygrometer Module
  Part3 = FC-28 Soil Hygrometer Module - Probe
  Power_plug1 = Power plug
  J1 = Piezo Speaker

nets:
  N1: U1.D0, U1.RST
  N2: U1.D1, DS3231_RTC_Module1.SCL
  N3: U1.D2, DS3231_RTC_Module1.SDA
  VCC: U1.3V3, DS3231_RTC_Module1.VCC, Part1.VCC, Part2.VCC
  GND: U1.GND, DS3231_RTC_Module1.GND, Part1.GND, Part2.GND, Power_plug1.GND, J1.pin1
  N4: U1.D5, Part1.SCK
  N5: U1.D6, Part1.MISO
  N6: U1.D7, Part1.MOSI
  N7: U1.D8, Part1.CS
  VIN: U1.Vin, Power_plug1.VCC
  N8: U1.A0, Part2.AO
  N9: Part2.POS, Part3.POS
  N10: Part2.NEG, Part3.NEG

notes:
  5VDC-9VDC
  Passive Buzzer
  DS3231 RTC Module
  MicroSD Card Adapter
  FC-28 Soil Hygrometer Module

custom parts:
  NodeMCU V3.0: ESP8266 based NodeMCU
  DS3231 RTC Module: The DS3231 RTC High Precision Real-Time Clock Module is a low-cost, extremely accurate I2C real-time clock (RTC), it is more accurate than the ds1307 as this module is integrated with temperature-compensated crystal oscillator (TCXO) and crystal. The device incorporates a battery input, and maintains accurate timekeeping when main power to the device is interrupted. The RTC maintains seconds,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
  FC-28 Soil Hygrometer Module: The FC-28 is a soil hygrometer module that uses the Texas Instruments LM393 comparator chip to provide an analog measurement of soil humidity. The digital output is high when soil moisture is over a certain threshold, as determined by adjusting the potentiometer.
  FC-28 Soil Hygrometer Module - Probe: The FC-28 is a soil hygrometer module that uses the Texas Instruments LM393 comparator chip to provide an analog measurement of soil humidity.
